// Logisim project HW1_RDBL12_S1_PhamNguyenCaoTrieu.circ as structural Verilog: 1 circuit, main circuit main
module main (
  input  Reset,
  input  CLK,
  output [3:0] Down
);

  wire d_ff_1_qn, d_ff_2_qn, d_ff_3_qn, d_ff_4_qn;

  D_Flip_Flop d_ff_1 (.D(d_ff_1_qn), .clk(CLK), .Q(Down[0]), .Qn(d_ff_1_qn), .preset(Reset));  // open: reset
  D_Flip_Flop d_ff_2 (.D(d_ff_2_qn), .clk(Down[0]), .Q(Down[1]), .Qn(d_ff_2_qn), .preset(Reset));  // open: reset
  D_Flip_Flop d_ff_3 (.D(d_ff_3_qn), .clk(Down[1]), .Q(Down[2]), .Qn(d_ff_3_qn), .preset(Reset));  // open: reset
  D_Flip_Flop d_ff_4 (.D(d_ff_4_qn), .clk(Down[2]), .Q(Down[3]), .Qn(d_ff_4_qn), .preset(Reset));  // open: reset

  // Notes on the sheet:
  //   Down: pull=down
endmodule
