// Logisim project HW2_RDBL12_S1_PhamNguyenCaoTrieu.circ as structural Verilog: 1 circuit, main circuit main
module main (
  input  clk,
  input  Reset,
  output [3:0] Decade
);

  wire and_1_out, d_ff_1_qn, d_ff_2_qn, d_ff_3_qn, d_ff_4_qn, or_1_out;

  D_Flip_Flop d_ff_1 (.D(d_ff_1_qn), .clk(clk), .Q(Decade[0]), .Qn(d_ff_1_qn), .reset(or_1_out));  // open: preset
  or or_1 (or_1_out, Reset, and_1_out);
  D_Flip_Flop d_ff_2 (.D(d_ff_2_qn), .clk(d_ff_1_qn), .Q(Decade[1]), .Qn(d_ff_2_qn), .reset(or_1_out));  // open: preset
  D_Flip_Flop d_ff_3 (.D(d_ff_3_qn), .clk(d_ff_2_qn), .Q(Decade[2]), .Qn(d_ff_3_qn), .reset(or_1_out));  // open: preset
  D_Flip_Flop d_ff_4 (.D(d_ff_4_qn), .clk(d_ff_3_qn), .Q(Decade[3]), .Qn(d_ff_4_qn), .reset(or_1_out));  // open: preset
  and and_1 (and_1_out, Decade[3], Decade[1]);

  // Notes on the sheet:
  //   Decade: pull=up
endmodule
